# Fritzing sketch schema (saved by Fritzing 0.9.0b)

parts:
  Part1 = Arduino Nano (Rev3.0)
  U1 = FS1000A - 433Mhz RF Transmitter [package=THT]
  U2 = ESP8266 WiFi Module [part_number=ESP8266]
  IC1 = Voltage Regulator AMS1117 [package=sot223]

nets:
  N1: Part1.D2, U2.TXD
  N2: Part1.D3, U2.RXD
  N3: Part1.D10, U1.DATA
  GND: Part1.GND, U1.GND, U2.GND, IC1.GND
  5V: Part1.5V, U1.VCC, IC1.IN
  N4: U2.VCC, U2.CH_PD, IC1.OUT

custom parts:
  FS1000A - 433Mhz RF Transmitter: This is 433Mhz RF transmitter with receiver kit for Arduino ARM MCU wireless Application environment: Remote control switch, receiver module, motorcycles, automobile anti-theft products, home security products, electric doors, shutter doors, windows, remote control socket, remote control LED, remote audio remote control electric doors, garage door remote control, remote control retractable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
  ESP8266 WiFi Module: Generic WiFi Module based on the ESP8266 with onboard PCB antenna and UART communications
